# Fritzing sketch ezekiel-raymond-assignment-wifi (saved by Fritzing 0.9.4)
breadboards: 2

parts:
  S3 = Pushbutton [package="[THT]"]
  S4 = Pushbutton [package="[THT]"]
  Part1 = Adafruit Feather HUZZAH ESP8266 [part_number="Adafruit #2821"]
  R2 = Resistor [tolerance=±5% resistance=220 package=THT]
  R4 = Resistor [tolerance=±5% resistance=220 package=THT]
  R6 = Resistor [tolerance=±5% resistance=220 package=THT]
  R7 = Resistor [tolerance=±5% resistance=220 package=THT]
  R8 = Resistor [tolerance=±5% resistance=220 package=THT]
  R9 = Resistor [tolerance=±5% resistance=220 package=THT]
  S5 = Pushbutton [package="[THT]"]
  Part2 = Adafruit Feather HUZZAH ESP8266 [part_number="Adafruit #2821"]  # not connected
  J1 = Piezo Speaker
  LED1 = LED - 5mm [color="Red (633nm)" package="5 mm [THT]"]
  LED2 = LED - 5mm [color="Red (633nm)" package="5 mm [THT]"]
  LED3 = LED - 5mm [color="Red (633nm)" package="5 mm [THT]"]

nets:
  N1: S3.Pin_1, S3.Pin_2, S4.Pin_1, S4.Pin_2, Part1.GND, R2.Pin_0, R6.Pin_0, R7.Pin_0, S5.Pin_1, S5.Pin_2, J1.pin2, LED2.cathode
  N2: S3.Pin_3, S3.Pin_4, Part1.GPIO0, R4.Pin_0
  N3: S4.Pin_3, S4.Pin_4, Part1.GPIO13/MOSI, R8.Pin_0
  N4: Part1.GPIO12/MISO, LED1.anode
  N5: Part1.GPIO14/SCK, J1.pin1
  N6: Part1.3.3V, R4.Pin_1, R8.Pin_1, R9.Pin_1
  N7: Part1.GPIO15, R6.Pin_1, LED2.anode
  N8: Part1.GPIO16, LED3.anode
  N9: Part1.GPIO2, R9.Pin_0, S5.Pin_3, S5.Pin_4
  N10: R2.Pin_1, LED1.cathode
  N11: R7.Pin_1, LED3.cathode

custom parts:
  Adafruit Feather HUZZAH ESP8266: his is the Adafruit Feather HUZZAH ESP8266 - our take on an 'all-in-one' ESP8266 WiFi development board with built in USB and battery charging. Its an ESP8266 WiFi module with all the extras you need, ready to rock! We have other boards in the Feather family, check'em out here. At the Feather HUZZAH's heart is an ESP8266 WiFi microcontroller clocked at 80 MHz and at 3.3V logic. This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
